# Fritzing sketch capitulo3 (saved by Fritzing 0.9.3b)
breadboards: 1

parts:
  Part1 = Arduino Uno (Rev3)
  R1 = Resistor [tolerance=±5% resistance=220 package=THT]
  LED1 = LED - 5mm [color="Red (633nm)" package="5 mm [THT]"]
  R2 = Resistor [tolerance=±5% resistance=220 package=THT]
  LED2 = LED - 5mm [color="Red (633nm)" package="5 mm [THT]"]
  R3 = Resistor [tolerance=±5% resistance=220 package=THT]
  LED3 = LED - 5mm [color="Red (633nm)" package="5 mm [THT]"]
  LED4 = LED - 5mm [color="Red (633nm)" package="5 mm [THT]"]
  R4 = Resistor [tolerance=±5% resistance=220 package=THT]

nets:
  N1: Part1.D2, LED4.anode
  N2: Part1.D3_PWM, Part1.D4, Part1.D5_PWM, Part1.GND, R1.Pin_0, R2.Pin_0, R3.Pin_0, R4.Pin_0
  N3: R1.Pin_1, LED1.cathode
  N4: R2.Pin_1, LED2.cathode
  N5: R3.Pin_1, LED4.cathode
  N6: LED3.cathode, R4.Pin_1
